// Logisim project main.circ as structural Verilog: 1 circuit, main circuit main
module main (
  output out_1,
  output out_2,
  output out_3,
  output out_4,
  output out_5,
  output out_6,
  output out_7,
  output out_8
);

  RAM #(.addrWidth(4)) ram_1 ();  // open: addr, data, sel, clk, ld, clr
endmodule
